# Fritzing sketch Schaltung (saved by Fritzing 1.0.3b)
breadboards: 1

parts:
  Bauteil1 = Arduino Nano (Rev3.0)
  4x20_LCD_screen_w/Red_Screen1 = 4x20 LCD screen w/Red Screen
  LCM1602_IIC1 = LCM1602 IIC [part_number="LCM1602 IIC" chip_label="LCM1602 IIC" package="DIP (Dual Inline) [THT]"]

nets:
  GND: Bauteil1.GND, LCM1602_IIC1.GND
  VIN: Bauteil1.VIN, LCM1602_IIC1.VCC
  N1: Bauteil1.A5, LCM1602_IIC1.SCL
  N2: Bauteil1.A4, LCM1602_IIC1.SDA
  VSS: 4x20_LCD_screen_w/Red_Screen1.VSS, LCM1602_IIC1.VSS
  VDD: 4x20_LCD_screen_w/Red_Screen1.VDD, LCM1602_IIC1.VDD
  N3: 4x20_LCD_screen_w/Red_Screen1.V0, LCM1602_IIC1.V0
  N4: 4x20_LCD_screen_w/Red_Screen1.RS, LCM1602_IIC1.RS
  N5: 4x20_LCD_screen_w/Red_Screen1.R/W, LCM1602_IIC1.RW
  N6: 4x20_LCD_screen_w/Red_Screen1.E, LCM1602_IIC1.E
  N7: 4x20_LCD_screen_w/Red_Screen1.DB0, LCM1602_IIC1.D0
  N8: 4x20_LCD_screen_w/Red_Screen1.DB1, LCM1602_IIC1.D1
  N9: 4x20_LCD_screen_w/Red_Screen1.DB2, LCM1602_IIC1.D2
  N10: 4x20_LCD_screen_w/Red_Screen1.DB3, LCM1602_IIC1.D3
  N11: 4x20_LCD_screen_w/Red_Screen1.DB4, LCM1602_IIC1.D4
  N12: 4x20_LCD_screen_w/Red_Screen1.DB5, LCM1602_IIC1.D5
  N13: 4x20_LCD_screen_w/Red_Screen1.DB6, LCM1602_IIC1.D6
  N14: 4x20_LCD_screen_w/Red_Screen1.DB7, LCM1602_IIC1.D7
  N15: 4x20_LCD_screen_w/Red_Screen1.LED+, LCM1602_IIC1.A
  N16: 4x20_LCD_screen_w/Red_Screen1.LED-, LCM1602_IIC1.K

custom parts:
  4x20 LCD screen w/Red Screen: A standard character display with 4x20 characters.
  LCM1602 IIC: I2C-Module to use a 1602 or 2004 LCD on with the wire.h libory Serial LCD Modul
